// Logisim project Pipeline.circ as structural Verilog: 4 circuits, main circuit main
module main (
  input  reset,
  input  [15:0] FL,
  input  [15:0] FH,
  input  [3:0] Symbol,
  input  [4:0] nsyms,
  input  Bool_Flag,
  output [15:0] RANGE,
  output [23:0] LOW
);

  wire Bool_Flag_q, Comp_Mux_1_2_q, Comp_Mux_1_q, general_clk_out, stage_1_1_bool_flag_2,
       stage_1_1_comp_mux_1, stage_2_1_comp_mux_1_2;
  wire [1:0] Bool_Symbol_q, stage_2_1_bool_symbol;
  wire [3:0] stage_1_1_symbol_2, Symbol_q;
  wire [4:0] CNT_q, D_q, stage_2_1_d, stage_3_1_cnt_2;
  wire [15:0] Initial_Range_q, LUT_U_q, LUT_V_q, Range_Ready_q, stage_1_1_lut_u, stage_1_1_lut_v,
       stage_1_1_uu, stage_1_1_vv, stage_2_1_initial_range, stage_2_1_range_ready, stage_2_1_u,
       stage_2_1_v_bool, stage_3_1_range, U_q, UU_q, V_Bool_q, VV_q;
  wire [23:0] stage_3_1_low_2;

  Clock general_clk (.out(general_clk_out));
  stage_1 stage_1_1 (
    .clk(general_clk_out), .reset(reset), .FL(FL), .FH(FH), .Symbol(Symbol),
    .Number_of_symbols__nsyms(nsyms), .Bool_Flag(Bool_Flag), .LUT_U(stage_1_1_lut_u),
    .LUT_V(stage_1_1_lut_v), .Symbol_2(stage_1_1_symbol_2), .UU(stage_1_1_uu), .VV(stage_1_1_vv),
    .COMP_Mux_1(stage_1_1_comp_mux_1), .Bool_Flag_2(stage_1_1_bool_flag_2));
  Register #(.width(16)) LUT_U (.D(stage_1_1_lut_u), .Q(LUT_U_q));  // open: en, clk, clr
  Register #(.width(16)) LUT_V (.D(stage_1_1_lut_v), .Q(LUT_V_q));  // open: en, clk, clr
  Register #(.width(4)) u_Symbol (.D(stage_1_1_symbol_2), .Q(Symbol_q));  // open: en, clk, clr
  Register #(.width(16)) UU (.D(stage_1_1_uu), .Q(UU_q));  // open: en, clk, clr
  Register #(.width(16)) VV (.D(stage_1_1_vv), .Q(VV_q));  // open: en, clk, clr
  Register #(.width(1)) Comp_Mux_1 (.D(stage_1_1_comp_mux_1), .Q(Comp_Mux_1_q));  // open: en, clk, clr
  Register #(.width(1)) u_Bool_Flag (.D(stage_1_1_bool_flag_2), .Q(Bool_Flag_q));  // open: en, clk, clr
  stage_2 stage_2_1 (
    .LUT_U(LUT_U_q), .LUT_V(LUT_V_q), .Symbol(Symbol_q), .UU(UU_q), .VV(VV_q), .Comp_Mux_1(Comp_Mux_1_q),
    .Bool_Flag(Bool_Flag_q), .Range(Range_Ready_q), .Comp_Mux_1_2(stage_2_1_comp_mux_1_2),
    .Bool_Symbol(stage_2_1_bool_symbol), .D(stage_2_1_d), .U(stage_2_1_u), .V_Bool(stage_2_1_v_bool),
    .Initial_Range(stage_2_1_initial_range), .Range_Ready(stage_2_1_range_ready));
  Register #(.width(1)) Comp_Mux_1_2 (.D(stage_2_1_comp_mux_1_2), .Q(Comp_Mux_1_2_q));  // open: en, clk, clr
  Register #(.width(2)) Bool_Symbol (.D(stage_2_1_bool_symbol), .Q(Bool_Symbol_q));  // open: en, clk, clr
  Register #(.width(5)) D (.D(stage_2_1_d), .Q(D_q));  // open: en, clk, clr
  Register #(.width(16)) U (.D(stage_2_1_u), .Q(U_q));  // open: en, clk, clr
  Register #(.width(16)) V_Bool (.D(stage_2_1_v_bool), .Q(V_Bool_q));  // open: en, clk, clr
  Register #(.width(16)) Initial_Range (.D(stage_2_1_initial_range), .Q(Initial_Range_q));  // open: en, clk, clr
  Register #(.width(16)) Range_Ready (.D(stage_2_1_range_ready), .Q(Range_Ready_q));  // open: en, clk, clr
  stage_3 stage_3_1 (
    .CNT(CNT_q), .Comp_Mux_1(Comp_Mux_1_2_q), .Bool_Symbol(Bool_Symbol_q), .D(D_q), .U(U_q),
    .V_Bool(V_Bool_q), .Initial_Range(Initial_Range_q), .Range_Ready(Range_Ready_q), .Low(LOW),
    .CNT_2(stage_3_1_cnt_2), .Range(stage_3_1_range), .Low_2(stage_3_1_low_2));
  Register #(.width(5)) CNT (.D(stage_3_1_cnt_2), .Q(CNT_q));  // open: en, clk, clr
  Register #(.width(16)) u_Range (.D(stage_3_1_range), .Q(RANGE));  // open: en, clk, clr
  Register #(.width(24)) u_Low (.D(stage_3_1_low_2), .Q(LOW));  // open: en, clk, clr
endmodule

// Stage 1
module stage_1 (
  input  clk,
  input  reset,
  input  [15:0] FL,
  input  [15:0] FH,
  input  [3:0] Symbol,
  input  [4:0] Number_of_symbols__nsyms,
  input  Bool_Flag,
  output [15:0] LUT_U,
  output [15:0] LUT_V,
  output [3:0] Symbol_2,
  output [15:0] UU,
  output [15:0] VV,
  output COMP_Mux_1,
  output Bool_Flag_2
);
endmodule

// Stage 2
module stage_2 (
  input  [15:0] LUT_U,
  input  [15:0] LUT_V,
  input  [3:0] Symbol,
  input  [15:0] UU,
  input  [15:0] VV,
  input  Comp_Mux_1,
  input  Bool_Flag,
  input  [15:0] Range,
  output Comp_Mux_1_2,
  output [1:0] Bool_Symbol,
  output [4:0] D,
  output [15:0] U,
  output [15:0] V_Bool,
  output [15:0] Initial_Range,
  output [15:0] Range_Ready
);
endmodule

// Stage 3
module stage_3 (
  input  [4:0] CNT,
  input  Comp_Mux_1,
  input  [1:0] Bool_Symbol,
  input  [4:0] D,
  input  [15:0] U,
  input  [15:0] V_Bool,
  input  [15:0] Initial_Range,
  input  [15:0] Range_Ready,
  input  [23:0] Low,
  output [4:0] CNT_2,
  output [15:0] Range,
  output [23:0] Low_2
);
endmodule
