// Logisim project Arq_pipeline.circ as structural Verilog: 7 circuits, main circuit main
module main (
  input  [15:0] FL,
  input  [15:0] FH,
  input  [3:0] Symb,
  input  [4:0] N_Syms,
  input  reset
);

  wire COMP_mux_1_q, Stage_1_comp_mux_1, Stage_4_comp_mux2, Stage_4_comp_mux3;
  wire [4:0] Stage_3_d, Stage_4_d_2;
  wire [15:0] LOW_2_q, LOW_q, multiplexer_2_out, RANGE_2_q, RANGE_q, Stage_1_uu, Stage_1_vv, Stage_2_low,
       Stage_2_range, Stage_3_low_2, Stage_3_range_2, Stage_4_low_2, Stage_4_range_2, Stage_5_out_low,
       Stage_5_out_range, UU_q, VV_q;
  wire [31:0] CNT_q, multiplexer_3_out, Stage_3_c_s0, Stage_3_in_cnt_2, Stage_3_m_s0, Stage_4_c_s0_2,
       Stage_4_c_s8, Stage_4_in_cnt_2, Stage_4_low_s8, Stage_4_m_s0_2, Stage_4_m_s8, Stage_4_s,
       Stage_5_out_cnt;

  stage_1 Stage_1 (
    .FL(FL), .FH(FH), .Symb(Symb), .N_Syms(N_Syms), .UU(Stage_1_uu), .COMP_mux_1(Stage_1_comp_mux_1),
    .VV(Stage_1_vv));
  Multiplexer #(.width(16), .enable("false")) multiplexer_1 (
    .in0(LOW_2_q), .in1({16{1'b0}}), .sel(reset));  // open: out
  Register #(.width(16)) UU (.D(Stage_1_uu), .Q(UU_q));  // open: en, clk, clr
  Register #(.width(1)) COMP_mux_1 (.D(Stage_1_comp_mux_1), .Q(COMP_mux_1_q));  // open: en, clk, clr
  Register #(.width(16)) VV (.D(Stage_1_vv), .Q(VV_q));  // open: en, clk, clr
  Multiplexer #(.width(16), .enable("false")) multiplexer_2 (
    .in0(RANGE_2_q), .in1(16'h8000), .out(multiplexer_2_out), .sel(reset));
  stage_2 Stage_2 (
    .UU(UU_q), .COMP_mux_1(COMP_mux_1_q), .VV(VV_q), .in_range(multiplexer_2_out), .LOW(Stage_2_low),
    .RANGE(Stage_2_range));  // open: in_low
  Register #(.width(16)) LOW (.D(Stage_2_low), .Q(LOW_q));  // open: en, clk, clr
  Register #(.width(16)) RANGE (.D(Stage_2_range), .Q(RANGE_q));  // open: en, clk, clr
  Multiplexer #(.width(32), .enable("false")) multiplexer_3 (
    .in0(CNT_q), .in1(32'hfffffff7), .out(multiplexer_3_out), .sel(reset));
  stage_3 Stage_3 (
    .LOW(LOW_q), .RANGE(RANGE_q), .in_cnt(multiplexer_3_out), .LOW_2(Stage_3_low_2),
    .RANGE_2(Stage_3_range_2), .in_cnt_2(Stage_3_in_cnt_2), .D(Stage_3_d), .C_s0(Stage_3_c_s0),
    .M_s0(Stage_3_m_s0));
  stage_4 Stage_4 (
    .LOW(Stage_3_low_2), .RANGE(Stage_3_range_2), .in_cnt(Stage_3_in_cnt_2), .D(Stage_3_d),
    .C_s0(Stage_3_c_s0), .M_s0(Stage_3_m_s0), .LOW_2(Stage_4_low_2), .RANGE_2(Stage_4_range_2),
    .in_cnt_2(Stage_4_in_cnt_2), .D_2(Stage_4_d_2), .COMP_mux2(Stage_4_comp_mux2), .S(Stage_4_s),
    .COMP_mux3(Stage_4_comp_mux3), .C_s0_2(Stage_4_c_s0_2), .M_s0_2(Stage_4_m_s0_2), .M_s8(Stage_4_m_s8),
    .C_s8(Stage_4_c_s8), .LOW_s8(Stage_4_low_s8));
  stage_5 Stage_5 (
    .LOW(Stage_4_low_2), .RANGE(Stage_4_range_2), .in_cnt(Stage_4_in_cnt_2), .D(Stage_4_d_2),
    .COMP_mux2(Stage_4_comp_mux2), .S(Stage_4_s), .COMP_mux3(Stage_4_comp_mux3), .C_s0(Stage_4_c_s0_2),
    .M_s0(Stage_4_m_s0_2), .M_s8(Stage_4_m_s8), .C_s8(Stage_4_c_s8), .LOW_s8(Stage_4_low_s8),
    .out_LOW(Stage_5_out_low), .out_RANGE(Stage_5_out_range), .out_CNT(Stage_5_out_cnt));
  Register #(.width(16)) LOW_2 (.D(Stage_5_out_low), .Q(LOW_2_q));  // open: en, clk, clr
  Register #(.width(16)) RANGE_2 (.D(Stage_5_out_range), .Q(RANGE_2_q));  // open: en, clk, clr
  Register #(.width(32)) CNT (.D(Stage_5_out_cnt), .Q(CNT_q));  // open: en, clk, clr
endmodule

module stage_1 (
  input  [15:0] FL,
  input  [15:0] FH,
  input  [3:0] Symb,
  input  [4:0] N_Syms,
  output [15:0] UU,
  output COMP_mux_1,
  output [15:0] VV
);

  wire [3:0] EC_PROB_SHIFT;
  wire [4:0] subtractor_1_out;
  wire [15:0] CDF_PROB_TOP, rom_1_data, rom_2_data, shifter_1_out, shifter_2_out, shifter_3_out,
       shifter_4_out;

  Comparator #(.width(16)) comparator_1 (.a(FL), .b(CDF_PROB_TOP), .lt(COMP_mux_1));  // open: gt, eq
  Subtractor #(.width(5)) subtractor_1 (.a(N_Syms), .b(5'b00001), .out(subtractor_1_out));  // open: bin, bout
  Shifter #(.width(16), .shift("lr")) shifter_1 (.in(FL), .\dist (EC_PROB_SHIFT), .out(shifter_1_out));
  Shifter #(.width(16), .shift("lr")) shifter_2 (.in(FH), .\dist (EC_PROB_SHIFT), .out(shifter_2_out));
  Shifter #(.width(16), .shift("lr")) shifter_3 (.in(shifter_1_out), .\dist (4'b0001), .out(shifter_3_out));
  Shifter #(.width(16), .shift("lr")) shifter_4 (.in(shifter_2_out), .\dist (4'b0001), .out(shifter_4_out));
  ROM #(.dataWidth(16)) rom_1 (.data(rom_1_data));  // open: addr, sel
  ROM #(.dataWidth(16)) rom_2 (.data(rom_2_data));  // open: addr, sel
  Adder #(.width(16)) adder_1 (.a(shifter_3_out), .b(rom_1_data), .out(UU));  // open: cin, cout
  Adder #(.width(16)) adder_2 (.a(shifter_4_out), .b(rom_2_data), .out(VV));  // open: cin, cout

  // Notes on the sheet:
  //   para melhorar o pipeline
  //   in_range e in_low poderiam ser recebidos no Stage 2
  //   Unir (nsyms - 1) com Symb
  //   Ligar no Addr das LUTs
  //   8 bits
endmodule

module stage_2 (
  input  [15:0] UU,
  input  COMP_mux_1,
  input  [15:0] VV,
  input  [15:0] in_range,
  input  [15:0] in_low,
  output [15:0] LOW,
  output [15:0] RANGE
);

  wire [15:0] multiplier_1_out, multiplier_2_out, multiplier_3_out, shifter_1_out, subtractor_1_out,
       subtractor_2_out, subtractor_3_out;

  Shifter #(.width(16), .shift("lr")) shifter_1 (.in(in_range), .\dist (4'b1000), .out(shifter_1_out));
  Subtractor #(.width(16)) subtractor_1 (.a(UU), .b(VV), .out(subtractor_1_out));  // open: bin, bout
  Multiplier #(.width(16)) multiplier_1 (.a(VV), .b(shifter_1_out), .out(multiplier_1_out));  // open: cin, cout
  Multiplier #(.width(16)) multiplier_2 (.a(UU), .b(shifter_1_out), .out(multiplier_2_out));  // open: cin, cout
  Subtractor #(.width(16)) subtractor_2 (
    .a(in_range), .b(multiplier_2_out), .out(subtractor_2_out));  // open: bin, bout
  Multiplier #(.width(16)) multiplier_3 (
    .a(subtractor_1_out), .b(shifter_1_out), .out(multiplier_3_out));  // open: cin, cout
  Subtractor #(.width(16)) subtractor_3 (
    .a(in_range), .b(multiplier_1_out), .out(subtractor_3_out));  // open: bin, bout
  Adder #(.width(16)) adder_1 (.a(subtractor_2_out), .b(in_low), .out(LOW));  // open: cin, cout
  Multiplexer #(.width(16), .enable("false")) multiplexer_1 (
    .in0(subtractor_3_out), .in1(multiplier_3_out), .out(RANGE), .sel(COMP_mux_1));
endmodule

module stage_3 (
  input  [15:0] LOW,
  input  [15:0] RANGE,
  input  [31:0] in_cnt,
  output [15:0] LOW_2,
  output [15:0] RANGE_2,
  output [31:0] in_cnt_2,
  output [4:0] D,
  output [31:0] C_s0,
  output [31:0] M_s0
);

  wire [4:0] _builtin_clz_output;
  wire [31:0] shifter_1_out;

  builtin_clz _builtin_clz (.RANGE(RANGE), .\output (_builtin_clz_output));
  Subtractor #(.width(5)) subtractor_1 (.a(5'b10000), .b(_builtin_clz_output), .out(D));  // open: bin, bout
  Adder #(.width(32)) adder_1 (.a(in_cnt), .b(32'hfffffff0), .out(C_s0));  // open: cin, cout
  Shifter #(.width(32)) shifter_1 (.in(32'h1), .\dist (C_s0[4:0]), .out(shifter_1_out));
  Subtractor #(.width(32)) subtractor_2 (.a(shifter_1_out), .b(32'h1), .out(M_s0));  // open: bin, bout
  // Pins of 5 and 32 bits meet at C_s0

  assign in_cnt_2 = in_cnt;
  assign LOW_2 = LOW;
  assign RANGE_2 = RANGE;
endmodule

module stage_4 (
  input  [15:0] LOW,
  input  [15:0] RANGE,
  input  [31:0] in_cnt,
  input  [4:0] D,
  input  [31:0] C_s0,
  input  [31:0] M_s0,
  output [15:0] LOW_2,
  output [15:0] RANGE_2,
  output [31:0] in_cnt_2,
  output [4:0] D_2,
  output COMP_mux2,
  output [31:0] S,
  output COMP_mux3,
  output [31:0] C_s0_2,
  output [31:0] M_s0_2,
  output [31:0] M_s8,
  output [31:0] C_s8,
  output [31:0] LOW_s8
);

  wire comparator_1_eq, comparator_1_gt, comparator_2_eq, comparator_2_gt;
  wire [31:0] bit_extender_1_out, bit_extender_2_out;

  Adder #(.width(32)) adder_1 (.a(in_cnt), .b(bit_extender_1_out), .out(S));  // open: cin, cout
  assign bit_extender_1_out = {{27{1'b0}}, D};  // Bit_Extender bit_extender_1
  Shifter #(.width(32), .shift("lr")) shifter_1 (.in(M_s0), .\dist (5'b01000), .out(M_s8));
  Subtractor #(.width(32)) subtractor_1 (.a(C_s0), .b(32'h8), .out(C_s8));  // open: bin, bout
  Comparator #(.width(32)) comparator_1 (
    .a(S), .b({32{1'b0}}), .gt(comparator_1_gt), .eq(comparator_1_eq));  // open: lt
  Comparator #(.width(32)) comparator_2 (.a(S), .b(32'h8), .gt(comparator_2_gt), .eq(comparator_2_eq));  // open: lt
  or or_1 (COMP_mux2, comparator_1_gt, comparator_1_eq);
  or or_2 (COMP_mux3, comparator_2_gt, comparator_2_eq);
  assign bit_extender_2_out = {{16{1'b0}}, LOW};  // Bit_Extender bit_extender_2
  assign LOW_s8 = bit_extender_2_out & M_s0;  // AND_Gate and_1, 32 bits wide

  assign C_s0_2 = C_s0;
  assign D_2 = D;
  assign in_cnt_2 = in_cnt;
  assign LOW_2 = LOW;
  assign M_s0_2 = M_s0;
  assign RANGE_2 = RANGE;
endmodule

module stage_5 (
  input  [15:0] LOW,
  input  [15:0] RANGE,
  input  [31:0] in_cnt,
  input  [4:0] D,
  input  COMP_mux2,
  input  [31:0] S,
  input  COMP_mux3,
  input  [31:0] C_s0,
  input  [31:0] M_s0,
  input  [31:0] M_s8,
  input  [31:0] C_s8,
  input  [31:0] LOW_s8,
  output [15:0] out_LOW,
  output [15:0] out_RANGE,
  output [31:0] out_CNT
);

  wire [31:0] adder_1_out, and_1_out, bit_extender_1_out, bit_extender_2_out, bit_extender_3_out,
       multiplexer_1_out, multiplexer_2_out, multiplexer_3_out, multiplexer_4_out, shifter_1_out,
       shifter_2_out, shifter_3_out, subtractor_1_out;

  assign bit_extender_1_out = {{16{1'b0}}, LOW};  // Bit_Extender bit_extender_1
  assign bit_extender_2_out = {{16{1'b0}}, RANGE};  // Bit_Extender bit_extender_2
  Multiplexer #(.width(32), .enable("false")) multiplexer_1 (
    .in0(M_s0), .in1(M_s8), .out(multiplexer_1_out), .sel(COMP_mux3));
  Multiplexer #(.width(32), .enable("false")) multiplexer_2 (
    .in0(bit_extender_1_out), .in1(LOW_s8), .out(multiplexer_2_out), .sel(COMP_mux3));
  Multiplexer #(.width(32), .enable("false")) multiplexer_3 (
    .in0(C_s0), .in1(C_s8), .out(multiplexer_3_out), .sel(COMP_mux3));
  assign and_1_out = multiplexer_2_out & multiplexer_1_out;  // AND_Gate and_1, 32 bits wide
  assign bit_extender_3_out = {{27{1'b0}}, D};  // Bit_Extender bit_extender_3
  Shifter #(.width(32)) shifter_1 (.in(bit_extender_1_out), .\dist (D), .out(shifter_1_out));
  Shifter #(.width(32)) shifter_2 (.in(and_1_out), .\dist (D), .out(shifter_2_out));
  Shifter #(.width(32)) shifter_3 (.in(bit_extender_2_out), .\dist (D), .out(shifter_3_out));
  Adder #(.width(32)) adder_1 (.a(multiplexer_3_out), .b(bit_extender_3_out), .out(adder_1_out));  // open: cin, cout
  Multiplexer #(.width(32), .enable("false")) multiplexer_4 (
    .in0(shifter_1_out), .in1(shifter_2_out), .out(multiplexer_4_out), .sel(COMP_mux2));
  Subtractor #(.width(32)) subtractor_1 (.a(adder_1_out), .b(32'h18), .out(subtractor_1_out));  // open: bin, bout
  Multiplexer #(.width(32), .enable("false")) multiplexer_5 (
    .in0(S), .in1(subtractor_1_out), .out(out_CNT), .sel(COMP_mux2));
  Bit_Extender #(.in_width(32)) bit_extender_4 (.in(multiplexer_4_out), .out(out_LOW));
  Bit_Extender #(.in_width(32)) bit_extender_5 (.in(shifter_3_out), .out(out_RANGE));

  // Notes on the sheet:
  //   MUX_3_m
  //   MUX_3_low
  //   MUX_3_c
  //   MUX_2_low
  //   MUX_2_cnt
endmodule

module builtin_clz (
  input  [15:0] RANGE,
  output [4:0] \output 
);

  wire [31:0] bit_extender_1_out;

  assign bit_extender_1_out = {{16{1'b0}}, RANGE};  // Bit_Extender bit_extender_1
endmodule
